// Logisim project hw3_10.circ as structural Verilog: 1 circuit, main circuit main
module main (
  input  x0,
  input  x1,
  input  y0,
  input  y1,
  output p0,
  output p1,
  output p2,
  output p3
);

  wire and_1_out, and_2_out, and_4_out, and_6_out;

  and and_1 (and_1_out, x0, y1);
  and and_2 (and_2_out, y0, x1);
  and and_3 (p3, x1, y1);
  and and_4 (and_4_out, p3, x0);
  and and_5 (p0, x0, y0);
  xor xor_1 (p1, and_1_out, and_2_out);
  and and_6 (and_6_out, p0, x1);
  or or_1 (p2, p3, and_4_out, and_6_out);
endmodule
