// Logisim project hw3_4_b_new.circ as structural Verilog: 4 circuits, main circuit majority
module majority (
  input  in_1,
  input  in_2,
  input  in_3,
  output out_4
);

  wire and_gate_1_out_3, and_gate_2_out_3, and_gate_3_out_3, or_gate_1_out_3;

  and_gate and_gate_1 (.in_1(in_1), .in_2(in_2), .out_3(and_gate_1_out_3));
  and_gate and_gate_2 (.in_1(in_2), .in_2(in_3), .out_3(and_gate_2_out_3));
  and_gate and_gate_3 (.in_1(in_1), .in_2(in_3), .out_3(and_gate_3_out_3));
  or_gate or_gate_1 (.in_1(and_gate_1_out_3), .in_2(and_gate_2_out_3), .out_3(or_gate_1_out_3));
  or_gate or_gate_2 (.in_1(or_gate_1_out_3), .in_2(and_gate_3_out_3), .out_3(out_4));
endmodule

module not_gate (
  input  in_1,
  output out_2
);

  nor nor_1 (out_2, in_1, in_1);
endmodule

module and_gate (
  input  in_1,
  input  in_2,
  output out_3
);

  wire not_gate_1_out_2, not_gate_2_out_2;

  not_gate not_gate_1 (.in_1(in_1), .out_2(not_gate_1_out_2));
  not_gate not_gate_2 (.in_1(in_2), .out_2(not_gate_2_out_2));
  nor nor_1 (out_3, not_gate_1_out_2, not_gate_2_out_2);
endmodule

module or_gate (
  input  in_1,
  input  in_2,
  output out_3
);

  wire and_gate_1_out_3, not_gate_1_out_2, not_gate_2_out_2;

  not_gate not_gate_1 (.in_1(in_2), .out_2(not_gate_1_out_2));
  not_gate not_gate_2 (.in_1(in_1), .out_2(not_gate_2_out_2));
  and_gate and_gate_1 (.in_1(not_gate_2_out_2), .in_2(not_gate_1_out_2), .out_3(and_gate_1_out_3));
  not_gate not_gate_3 (.in_1(and_gate_1_out_3), .out_2(out_3));
endmodule
