// Logisim project hw3_4a.circ as structural Verilog: 1 circuit, main circuit main
module main (
  input  a,
  input  b,
  input  c,
  output out_4
);

  wire and_1_out, and_2_out, and_3_out, or_1_out;

  and and_1 (and_1_out, a, b);
  and and_2 (and_2_out, c, a);
  and and_3 (and_3_out, b, c);
  or or_1 (or_1_out, and_1_out, and_2_out);
  or or_2 (out_4, or_1_out, and_3_out);
endmodule
