// Logisim project hw3_4b.circ as structural Verilog: 1 circuit, main circuit main
module main (
  input  b,
  input  in_2,
  input  c,
  output out_4
);

  wire nor_1_out;

  nor nor_1 (nor_1_out, b, in_2);
  nor nor_2 (out_4, nor_1_out, c);

  // Notes on the sheet:
  //   a
endmodule
