// Logisim project hw3_4c_4d.circ as structural Verilog
module implication (
  input  a,
  input  b,
  output a__b
);

  wire not_1_out;

  not not_1 (not_1_out, a);
  or or_1 (a__b, not_1_out, b);
endmodule

module equivalence (
  input  in_1,
  input  in_2,
  output out_3
);

  wire implication_1_a__b, implication_2_a__b;

  implication implication_1 (.a(in_1), .b(in_2), .a__b(implication_1_a__b));
  implication implication_2 (.a(in_1), .b(in_2), .a__b(implication_2_a__b));
  buf and_1 (out_3, implication_2_a__b);  // AND_Gate
endmodule

module majority_4d (
  input  a,
  input  b,
  input  c,
  output majority
);

  wire and_1_out, and_2_out, and_3_out, equivalence_1_out_3, equivalence_2_out_3, equivalence_3_out_3,
       true_1__1;

  and and_1 (and_1_out, a, b);
  and and_2 (and_2_out, b, c);
  and and_3 (and_3_out, a, c);
  true true_1 (.A(c), ._1(true_1__1));
  equivalence equivalence_1 (.in_1(and_2_out), .in_2(true_1__1), .out_3(equivalence_1_out_3));
  equivalence equivalence_2 (.in_1(true_1__1), .in_2(and_1_out), .out_3(equivalence_2_out_3));
  equivalence equivalence_3 (.in_1(and_3_out), .in_2(true_1__1), .out_3(equivalence_3_out_3));
  and and_4 (majority, equivalence_2_out_3, equivalence_1_out_3, equivalence_3_out_3);
endmodule

module majority_4c (
  input  a,
  input  b,
  input  c,
  output majority
);

  wire implication_1_a__b, implication_2_a__b;

  implication implication_1 (.a(a), .b(b), .a__b(implication_1_a__b));
  implication implication_2 (.a(b), .b(c), .a__b(implication_2_a__b));
  implication implication_3 (.a(implication_1_a__b), .b(implication_2_a__b), .a__b(majority));
endmodule

module true (
  input  A,
  output _1
);

  wire not_1_out;

  not not_1 (not_1_out, A);
  or or_1 (_1, not_1_out, A);
endmodule
