// Logisim project hw3_7.circ as structural Verilog: 1 circuit, main circuit main
module main (
  input  b1,
  input  b2,
  input  b3,
  input  b4,
  output g1,
  output g2,
  output g3,
  output g4
);

  wire nand_1_out, nand_2_out, nand_3_out, nand_4_out, nand_5_out, nand_6_out, nand_7_out, nand_8_out,
       nand_9_out, nand_11_out;

  nand nand_1 (nand_1_out, b1, b1);
  nand nand_2 (nand_2_out, b2, b2);
  nand nand_3 (nand_3_out, b4, b4);
  nand nand_4 (nand_4_out, b3, b3);
  nand nand_5 (nand_5_out, nand_2_out, b3);
  nand nand_6 (nand_6_out, nand_1_out, b4);
  nand nand_7 (nand_7_out, nand_1_out, b2);
  nand nand_8 (nand_8_out, nand_4_out, b1);
  nand nand_9 (nand_9_out, nand_4_out, b3);
  nand nand_10 (g3, nand_5_out, nand_6_out);
  nand nand_11 (nand_11_out, b2, nand_3_out);
  nand nand_12 (g1, nand_8_out, nand_11_out);
  nand nand_13 (g2, nand_7_out, nand_9_out);

  assign g4 = b4;

  // Notes on the sheet:
  //   n1
  //   n2
  //   n4
  //   n3
  //   b3 n2
  //   b2 n1
  //   n1 b4
  //   b1 n3
  //   b3 n3
  //   b2 n4
endmodule
