// Logisim project hw3_8.circ as structural Verilog: 3 circuits, main circuit hw3_8a
module hw3_8a (
  input  A,
  input  B,
  output D,
  output C
);

  wire and_1_out, and_2_out, not_1_out, not_2_out;

  not not_1 (not_1_out, A);
  not not_2 (not_2_out, B);
  and and_1 (and_1_out, not_1_out, not_2_out);
  and and_2 (and_2_out, A, B);
  and and_3 (C, not_1_out, B);
  or or_1 (D, and_1_out, and_2_out);
endmodule

module hw3_8b (
  input  A,
  input  B,
  input  B_in,
  output D1_prime,
  output D1,
  output B_out
);

  wire hw3_8a_1_c, hw3_8a_1_d, nand_2_out, nand_3_out;

  hw3_8a hw3_8a_1 (.A(A), .B(B), .D(hw3_8a_1_d), .C(hw3_8a_1_c));
  hw3_8a hw3_8a_2 (.A(hw3_8a_1_d), .B(B_in), .D(D1));  // open: C
  nand nand_1 (D1_prime, hw3_8a_1_c, hw3_8a_1_c);
  nand nand_2 (nand_2_out, hw3_8a_1_c, hw3_8a_1_c);
  nand nand_3 (nand_3_out, D1_prime, B_in);
  nand nand_4 (B_out, nand_2_out, nand_3_out);
endmodule

module hw3_8c (
  input  x1,
  input  x2,
  input  x3,
  input  x4,
  input  y1,
  input  y2,
  input  y3,
  input  y4,
  output d1,
  output d2,
  output d3,
  output d4,
  output zero_result
);

  wire and_1_out, hw3_8b_1_d1, hw3_8b_1_d1_prime, hw3_8b_2_d1, hw3_8b_2_d1_prime, hw3_8b_3_d1,
       hw3_8b_3_d1_prime, hw3_8b_4_b_out, hw3_8b_4_d1, hw3_8b_4_d1_prime, not_1_out, not_2_out;

  not not_1 (not_1_out, y4);
  and and_1 (and_1_out, y4, not_1_out);
  hw3_8b hw3_8b_1 (
    .A(x4), .B(y4), .B_in(and_1_out), .D1_prime(hw3_8b_1_d1_prime), .D1(hw3_8b_1_d1), .B_out(hw3_8b_1_d1));
  hw3_8b hw3_8b_2 (
    .A(x3), .B(y3), .B_in(hw3_8b_1_d1), .D1_prime(hw3_8b_2_d1_prime), .D1(hw3_8b_2_d1), .B_out(hw3_8b_2_d1));
  hw3_8b hw3_8b_3 (
    .A(x2), .B(y2), .B_in(hw3_8b_2_d1), .D1_prime(hw3_8b_3_d1_prime), .D1(hw3_8b_3_d1), .B_out(hw3_8b_3_d1));
  hw3_8b hw3_8b_4 (
    .A(x1), .B(y1), .B_in(hw3_8b_3_d1), .D1_prime(hw3_8b_4_d1_prime), .D1(hw3_8b_4_d1), .B_out(hw3_8b_4_b_out));
  not not_2 (not_2_out, hw3_8b_4_b_out);
  buf and_2 (d1, not_2_out);  // AND_Gate
  and and_3 (d2, hw3_8b_3_d1, not_2_out);
  buf and_4 (d3, not_2_out);  // AND_Gate
  and and_5 (d4, not_2_out, hw3_8b_1_d1);
  nor nor_1 (zero_result, hw3_8b_1_d1_prime, hw3_8b_2_d1_prime, hw3_8b_3_d1_prime, hw3_8b_4_d1_prime);
endmodule
