// Logisim project hw3_8a_8b.circ as structural Verilog: 2 circuits, main circuit hw3_8a
module hw3_8a (
  input  A,
  input  B,
  output D,
  output C
);

  wire and_1_out, and_2_out, not_1_out, not_2_out;

  not not_1 (not_1_out, A);
  not not_2 (not_2_out, B);
  and and_1 (and_1_out, not_1_out, not_2_out);
  and and_2 (and_2_out, A, B);
  and and_3 (C, not_1_out, B);
  or or_1 (D, and_1_out, and_2_out);
endmodule

module hw3_8b (
  input  A,
  input  B,
  input  B_in,
  output D1_prime,
  output D1,
  output B_out
);

  wire hw3_8a_1_c, hw3_8a_1_d, nand_2_out, nand_3_out;

  hw3_8a hw3_8a_1 (.A(A), .B(B), .D(hw3_8a_1_d), .C(hw3_8a_1_c));
  hw3_8a hw3_8a_2 (.A(hw3_8a_1_d), .B(B_in), .D(D1));  // open: C
  nand nand_1 (D1_prime, hw3_8a_1_c, hw3_8a_1_c);
  nand nand_2 (nand_2_out, hw3_8a_1_c, hw3_8a_1_c);
  nand nand_3 (nand_3_out, D1_prime, B_in);
  nand nand_4 (B_out, nand_2_out, nand_3_out);
endmodule
