// Logisim project hw3_9.circ as structural Verilog: 1 circuit, main circuit main
module main (
  input  x0,
  input  x1,
  input  y0,
  input  y1,
  output p0,
  output p1,
  output p2,
  output p3
);

  wire and_1_out, and_3_out, and_4_out, and_5_out;

  and and_1 (and_1_out, x0, y1);
  and and_2 (p0, x0, y0);
  and and_3 (and_3_out, x1, y0);
  and and_4 (and_4_out, x1, y1);
  and and_5 (and_5_out, and_1_out, and_3_out);
  xor xor_1 (p1, and_1_out, and_3_out);
  xor xor_2 (p2, and_5_out, and_4_out);
  and and_6 (p3, and_5_out, and_4_out);
endmodule
